# Fritzing sketch ChickenFan2 (saved by Fritzing 0.9.2b)
circuit board: 10.1cm x 2.54cm
breadboards: 1

parts:
  47k = Resistor [tolerance=±5% resistance=220 package=THT]
  Nano1 = Arduino Nano v2.3
  ToRelay = Header 3 [package=jst-3-pth]
  Power = Header 3 [package=jst-3-pth]
  T1 = LM35 Temperature Sensor [package="TO92 [THT]"]
  ToFan = Header 3 [package=jst-3-pth]  # not connected

nets:
  N1: 47k.Pin_0, Nano1.D7, T1.Vout
  N2: 47k.Pin_1, Nano1.+5V, ToRelay.2, T1.+Vs
  GND: Nano1.GND, ToRelay.1, Power.3, T1.GND
  N3: Nano1.D2, ToRelay.3
  N4: Nano1.VIN, Power.1
